// Logisim project cpudesign.circ as structural Verilog: 24 circuits, main circuit NOTcmos
module NOTcmos (
  input  A,
  output C
);

  NANDcmos nandcmos_1 (.A(A), .B(A), .C(C));
endmodule

module NORcmos (
  input  A,
  input  B,
  output C
);

  wire nandcmos_1_c, nandcmos_2_c, nandcmos_3_c;

  NANDcmos nandcmos_1 (.A(A), .B(A), .C(nandcmos_1_c));
  NANDcmos nandcmos_2 (.A(B), .B(B), .C(nandcmos_2_c));
  NANDcmos nandcmos_3 (.A(nandcmos_1_c), .B(nandcmos_2_c), .C(nandcmos_3_c));
  NANDcmos nandcmos_4 (.A(nandcmos_3_c), .B(nandcmos_3_c), .C(C));
endmodule

module ORcmos (
  input  A,
  input  B,
  output C
);

  wire nandcmos_1_c, nandcmos_2_c;

  NANDcmos nandcmos_1 (.A(A), .B(A), .C(nandcmos_1_c));
  NANDcmos nandcmos_2 (.A(B), .B(B), .C(nandcmos_2_c));
  NANDcmos nandcmos_3 (.A(nandcmos_1_c), .B(nandcmos_2_c), .C(C));
endmodule

module NANDcmos (
  input  A,
  input  B,
  output C
);

  wire transistor_4_out;

  Transistor transistor_1 (.in(1'b1), .out(C), .gate(A));
  Transistor transistor_2 (.in(1'b1), .out(C), .gate(B));
  Transistor #(.\type ("n")) transistor_3 (.in(transistor_4_out), .out(C), .gate(A));
  Transistor #(.\type ("n")) transistor_4 (.in(1'b0), .out(transistor_4_out), .gate(B));
endmodule

module ANDcmos (
  input  in_1,
  input  in_2,
  output C
);

  wire nandcmos_1_c;

  NANDcmos nandcmos_1 (.A(in_1), .B(in_2), .C(nandcmos_1_c));
  NANDcmos nandcmos_2 (.A(nandcmos_1_c), .B(nandcmos_1_c), .C(C));
endmodule

module XORcmos (
  input  A,
  input  B,
  output C
);

  wire nandcmos_1_c, nandcmos_2_c, nandcmos_3_c, nandcmos_4_c;

  NANDcmos nandcmos_1 (.A(A), .B(A), .C(nandcmos_1_c));
  NANDcmos nandcmos_2 (.A(B), .B(B), .C(nandcmos_2_c));
  NANDcmos nandcmos_3 (.A(nandcmos_1_c), .B(B), .C(nandcmos_3_c));
  NANDcmos nandcmos_4 (.A(nandcmos_2_c), .B(A), .C(nandcmos_4_c));
  NANDcmos nandcmos_5 (.A(nandcmos_3_c), .B(nandcmos_4_c), .C(C));
endmodule

module halfadder (
  input  A,
  input  B,
  output S,
  output Cout
);

  XORcmos xorcmos_1 (.A(A), .B(B), .C(S));
  ANDcmos andcmos_1 (.in_1(A), .in_2(B), .C(Cout));
endmodule

module fulladder (
  input  A,
  input  B,
  input  Cin,
  output Sout,
  output Cout
);

  wire halfadder_1_cout, halfadder_1_s, halfadder_2_cout;

  halfadder halfadder_1 (.A(A), .B(B), .S(halfadder_1_s), .Cout(halfadder_1_cout));
  halfadder halfadder_2 (.A(halfadder_1_s), .B(Cin), .S(Sout), .Cout(halfadder_2_cout));
  ORcmos orcmos_1 (.A(halfadder_2_cout), .B(halfadder_1_cout), .C(Cout));
endmodule

module mux (
  input  A,
  input  Cin,
  output muxout
);

  XORcmos xorcmos_1 (.A(A), .B(Cin), .C(muxout));
endmodule

module fourbitadder (
  input  sign,
  input  A3,
  input  A2,
  input  A1,
  input  A0,
  input  B3,
  input  B2,
  input  B1,
  input  B0,
  input  Cin,
  output S0,
  output S1,
  output S2,
  output S3,
  output Cout,
  output overflow
);

  wire andcmos_1_c, andcmos_2_c, fulladder_1_cout, fulladder_2_cout, fulladder_3_cout, mux_1_muxout,
       mux_2_muxout, mux_3_muxout, mux_4_muxout, notcmos_1_c, xorcmos_1_c, xorcmos_2_c;

  mux mux_1 (.A(B0), .Cin(Cin), .muxout(mux_1_muxout));
  fulladder fulladder_1 (.A(A0), .B(mux_1_muxout), .Cin(Cin), .Sout(S0), .Cout(fulladder_1_cout));
  mux mux_2 (.A(B1), .Cin(Cin), .muxout(mux_2_muxout));
  fulladder fulladder_2 (.A(A1), .B(mux_2_muxout), .Cin(fulladder_1_cout), .Sout(S1), .Cout(fulladder_2_cout));
  mux mux_3 (.A(B2), .Cin(Cin), .muxout(mux_3_muxout));
  fulladder fulladder_3 (.A(A2), .B(mux_3_muxout), .Cin(fulladder_2_cout), .Sout(S2), .Cout(fulladder_3_cout));
  mux mux_4 (.A(B3), .Cin(Cin), .muxout(mux_4_muxout));
  fulladder fulladder_4 (.A(A3), .B(mux_4_muxout), .Cin(fulladder_3_cout), .Sout(S3), .Cout(Cout));
  XORcmos xorcmos_1 (.A(fulladder_3_cout), .B(Cout), .C(xorcmos_1_c));
  XORcmos xorcmos_2 (.A(Cin), .B(Cout), .C(xorcmos_2_c));
  NOTcmos notcmos_1 (.A(sign), .C(notcmos_1_c));
  ANDcmos andcmos_1 (.in_1(notcmos_1_c), .in_2(xorcmos_2_c), .C(andcmos_1_c));
  ANDcmos andcmos_2 (.in_1(sign), .in_2(xorcmos_1_c), .C(andcmos_2_c));
  ORcmos orcmos_1 (.A(andcmos_1_c), .B(andcmos_2_c), .C(overflow));
endmodule

module eightOR (
  input  in_1,
  input  in_2,
  input  in_3,
  input  in_4,
  input  in_5,
  input  in_6,
  input  in_7,
  input  in_8,
  output out_9
);

  wire orcmos_1_c, orcmos_2_c, orcmos_3_c, orcmos_4_c, orcmos_5_c, orcmos_6_c;

  ORcmos orcmos_1 (.A(in_1), .B(in_2), .C(orcmos_1_c));
  ORcmos orcmos_2 (.A(in_3), .B(in_4), .C(orcmos_2_c));
  ORcmos orcmos_3 (.A(in_5), .B(in_6), .C(orcmos_3_c));
  ORcmos orcmos_4 (.A(in_7), .B(in_8), .C(orcmos_4_c));
  ORcmos orcmos_5 (.A(orcmos_1_c), .B(orcmos_2_c), .C(orcmos_5_c));
  ORcmos orcmos_6 (.A(orcmos_3_c), .B(orcmos_4_c), .C(orcmos_6_c));
  ORcmos orcmos_7 (.A(orcmos_5_c), .B(orcmos_6_c), .C(out_9));
endmodule

module unsignedinput (
  input  A,
  input  B,
  input  C,
  input  D,
  input  E,
  input  F,
  input  G,
  input  H,
  input  I,
  input  J,
  input  K,
  input  L,
  input  M,
  input  N,
  input  O,
  input  P,
  output B3,
  output B2,
  output B1,
  output B0
);

  eightOR eightor_1 (.in_1(I), .in_2(J), .in_3(K), .in_4(L), .in_5(M), .in_6(N), .in_7(O), .in_8(P), .out_9(B3));
  eightOR eightor_2 (.in_1(F), .in_2(G), .in_3(H), .in_4(M), .in_5(N), .in_6(O), .in_7(P), .in_8(E), .out_9(B2));
  eightOR eightor_3 (.in_1(C), .in_2(D), .in_3(G), .in_4(H), .in_5(K), .in_6(L), .in_7(O), .in_8(P), .out_9(B1));
  eightOR eightor_4 (.in_1(B), .in_2(D), .in_3(F), .in_4(H), .in_5(J), .in_6(L), .in_7(N), .in_8(P), .out_9(B0));
endmodule

module signedinput (
  input  A,
  input  B,
  input  C,
  input  D,
  input  E,
  input  F,
  input  G,
  input  H,
  input  I,
  input  J,
  input  K,
  input  L,
  input  M,
  input  N,
  input  O,
  input  P,
  output B3,
  output B2,
  output B1,
  output B0
);

  eightOR eightor_1 (.in_1(A), .in_2(B), .in_3(C), .in_4(D), .in_5(E), .in_6(F), .in_7(G), .in_8(H), .out_9(B3));
  eightOR eightor_2 (.in_1(E), .in_2(F), .in_3(G), .in_4(H), .in_5(M), .in_6(N), .in_7(O), .in_8(P), .out_9(B2));
  eightOR eightor_3 (.in_1(C), .in_2(D), .in_3(G), .in_4(H), .in_5(K), .in_6(L), .in_7(O), .in_8(P), .out_9(B1));
  eightOR eightor_4 (.in_1(B), .in_2(D), .in_3(F), .in_4(H), .in_5(J), .in_6(L), .in_7(N), .in_8(P), .out_9(B0));
endmodule

module signmux4bit (
  input  sign,
  input  A3,
  input  A2,
  input  A1,
  input  A0,
  input  B3,
  input  B2,
  input  B1,
  input  B0,
  output C3,
  output C2,
  output C1,
  output C0
);

  wire andcmos_1_c, andcmos_2_c, andcmos_3_c, andcmos_4_c, andcmos_5_c, andcmos_6_c, andcmos_7_c,
       andcmos_8_c, notcmos_1_c;

  NOTcmos notcmos_1 (.A(sign), .C(notcmos_1_c));
  ANDcmos andcmos_1 (.in_1(B3), .in_2(sign), .C(andcmos_1_c));
  ANDcmos andcmos_2 (.in_1(B2), .in_2(sign), .C(andcmos_2_c));
  ANDcmos andcmos_3 (.in_1(B1), .in_2(sign), .C(andcmos_3_c));
  ANDcmos andcmos_4 (.in_1(B0), .in_2(sign), .C(andcmos_4_c));
  ANDcmos andcmos_5 (.in_1(A3), .in_2(notcmos_1_c), .C(andcmos_5_c));
  ANDcmos andcmos_6 (.in_1(A2), .in_2(notcmos_1_c), .C(andcmos_6_c));
  ANDcmos andcmos_7 (.in_1(A1), .in_2(notcmos_1_c), .C(andcmos_7_c));
  ANDcmos andcmos_8 (.in_1(A0), .in_2(notcmos_1_c), .C(andcmos_8_c));
  ORcmos orcmos_1 (.A(andcmos_5_c), .B(andcmos_1_c), .C(C3));
  ORcmos orcmos_2 (.A(andcmos_6_c), .B(andcmos_2_c), .C(C2));
  ORcmos orcmos_3 (.A(andcmos_7_c), .B(andcmos_3_c), .C(C1));
  ORcmos orcmos_4 (.A(andcmos_8_c), .B(andcmos_4_c), .C(C0));
endmodule

module fourAND (
  input  in_1,
  input  in_2,
  input  in_3,
  input  in_4,
  output out_5
);

  wire andcmos_1_c, andcmos_2_c;

  ANDcmos andcmos_1 (.in_1(in_1), .in_2(in_2), .C(andcmos_1_c));
  ANDcmos andcmos_2 (.in_1(in_3), .in_2(in_4), .C(andcmos_2_c));
  ANDcmos andcmos_3 (.in_1(andcmos_1_c), .in_2(andcmos_2_c), .C(out_5));
endmodule

module unsignedoutput (
  input  B3,
  input  B2,
  input  B1,
  input  B0,
  output A,
  output B,
  output C,
  output D,
  output E,
  output F,
  output G,
  output H,
  output I,
  output J,
  output K,
  output L,
  output M,
  output N,
  output O,
  output P
);

  wire notcmos_1_c, notcmos_2_c, notcmos_3_c, notcmos_4_c;

  NOTcmos notcmos_1 (.A(B3), .C(notcmos_1_c));
  NOTcmos notcmos_2 (.A(B2), .C(notcmos_2_c));
  NOTcmos notcmos_3 (.A(B1), .C(notcmos_3_c));
  NOTcmos notcmos_4 (.A(B0), .C(notcmos_4_c));
  fourAND fourand_1 (.in_1(notcmos_1_c), .in_2(notcmos_2_c), .in_3(notcmos_3_c), .in_4(notcmos_4_c), .out_5(A));
  fourAND fourand_2 (.in_1(B0), .in_2(notcmos_1_c), .in_3(notcmos_2_c), .in_4(notcmos_3_c), .out_5(B));
  fourAND fourand_3 (.in_1(notcmos_1_c), .in_2(B1), .in_3(notcmos_2_c), .in_4(notcmos_4_c), .out_5(C));
  fourAND fourand_4 (.in_1(B0), .in_2(B1), .in_3(notcmos_2_c), .in_4(notcmos_1_c), .out_5(D));
  fourAND fourand_5 (.in_1(notcmos_4_c), .in_2(notcmos_3_c), .in_3(B2), .in_4(notcmos_1_c), .out_5(E));
  fourAND fourand_6 (.in_1(B0), .in_2(notcmos_3_c), .in_3(B2), .in_4(notcmos_1_c), .out_5(F));
  fourAND fourand_7 (.in_1(notcmos_4_c), .in_2(B1), .in_3(B2), .in_4(notcmos_1_c), .out_5(G));
  fourAND fourand_8 (.in_1(B0), .in_2(B1), .in_3(B2), .in_4(notcmos_1_c), .out_5(H));
  fourAND fourand_9 (.in_1(B3), .in_2(notcmos_2_c), .in_3(notcmos_3_c), .in_4(notcmos_4_c), .out_5(I));
  fourAND fourand_10 (.in_1(B3), .in_2(notcmos_2_c), .in_3(notcmos_3_c), .in_4(B0), .out_5(J));
  fourAND fourand_11 (.in_1(B3), .in_2(notcmos_2_c), .in_3(B1), .in_4(notcmos_4_c), .out_5(K));
  fourAND fourand_12 (.in_1(B3), .in_2(notcmos_2_c), .in_3(B1), .in_4(B0), .out_5(L));
  fourAND fourand_13 (.in_1(B3), .in_2(B2), .in_3(notcmos_3_c), .in_4(notcmos_4_c), .out_5(M));
  fourAND fourand_14 (.in_1(B3), .in_2(B2), .in_3(notcmos_3_c), .in_4(B0), .out_5(N));
  fourAND fourand_15 (.in_1(B3), .in_2(B2), .in_3(B1), .in_4(notcmos_4_c), .out_5(O));
  fourAND fourand_16 (.in_1(B3), .in_2(B2), .in_3(B1), .in_4(B0), .out_5(P));
endmodule

module signedoutput (
  input  B3,
  input  B2,
  input  B1,
  input  B0,
  output A,
  output B,
  output C,
  output D,
  output E,
  output F,
  output G,
  output H,
  output I,
  output J,
  output K,
  output L,
  output M,
  output N,
  output O,
  output P
);

  wire notcmos_1_c, notcmos_2_c, notcmos_3_c, notcmos_4_c;

  NOTcmos notcmos_1 (.A(B3), .C(notcmos_1_c));
  NOTcmos notcmos_2 (.A(B2), .C(notcmos_2_c));
  NOTcmos notcmos_3 (.A(B1), .C(notcmos_3_c));
  NOTcmos notcmos_4 (.A(B0), .C(notcmos_4_c));
  fourAND fourand_1 (.in_1(B3), .in_2(notcmos_2_c), .in_3(notcmos_3_c), .in_4(notcmos_4_c), .out_5(A));
  fourAND fourand_2 (.in_1(B3), .in_2(notcmos_2_c), .in_3(notcmos_3_c), .in_4(B0), .out_5(B));
  fourAND fourand_3 (.in_1(B3), .in_2(notcmos_2_c), .in_3(B1), .in_4(notcmos_4_c), .out_5(C));
  fourAND fourand_4 (.in_1(B3), .in_2(B1), .in_3(notcmos_2_c), .in_4(B0), .out_5(D));
  fourAND fourand_5 (.in_1(B3), .in_2(B2), .in_3(notcmos_3_c), .in_4(notcmos_4_c), .out_5(E));
  fourAND fourand_6 (.in_1(B3), .in_2(B2), .in_3(notcmos_3_c), .in_4(B0), .out_5(F));
  fourAND fourand_7 (.in_1(B3), .in_2(B2), .in_3(B1), .in_4(notcmos_4_c), .out_5(G));
  fourAND fourand_8 (.in_1(B3), .in_2(B2), .in_3(B1), .in_4(B0), .out_5(H));
  fourAND fourand_9 (.in_1(notcmos_1_c), .in_2(notcmos_2_c), .in_3(notcmos_3_c), .in_4(notcmos_4_c), .out_5(I));
  fourAND fourand_10 (.in_1(notcmos_1_c), .in_2(notcmos_2_c), .in_3(notcmos_3_c), .in_4(B0), .out_5(J));
  fourAND fourand_11 (.in_1(notcmos_1_c), .in_2(notcmos_2_c), .in_3(B1), .in_4(notcmos_4_c), .out_5(K));
  fourAND fourand_12 (.in_1(notcmos_1_c), .in_2(notcmos_2_c), .in_3(B1), .in_4(B0), .out_5(L));
  fourAND fourand_13 (.in_1(notcmos_1_c), .in_2(B2), .in_3(notcmos_3_c), .in_4(notcmos_4_c), .out_5(M));
  fourAND fourand_14 (.in_1(notcmos_1_c), .in_2(B2), .in_3(notcmos_3_c), .in_4(B0), .out_5(N));
  fourAND fourand_15 (.in_1(notcmos_1_c), .in_2(B2), .in_3(B1), .in_4(notcmos_4_c), .out_5(O));
  fourAND fourand_16 (.in_1(notcmos_1_c), .in_2(B2), .in_3(B1), .in_4(B0), .out_5(P));
endmodule

module signmux16bit (
  input  sign,
  input  A0,
  input  A1,
  input  B0,
  input  B1,
  input  C0,
  input  C1,
  input  D0,
  input  D1,
  input  E0,
  input  E1,
  input  F0,
  input  F1,
  input  G0,
  input  G1,
  input  H0,
  input  H1,
  input  I0,
  input  I1,
  input  J0,
  input  J1,
  input  K0,
  input  K1,
  input  L0,
  input  L1,
  input  M0,
  input  M1,
  input  N0,
  input  N1,
  input  O0,
  input  O1,
  input  P0,
  input  P1,
  output A,
  output B,
  output C,
  output D,
  output E,
  output F,
  output G,
  output H,
  output I,
  output J,
  output K,
  output L,
  output M,
  output N,
  output O,
  output P
);

  signmux4bit signmux4bit_1 (
    .sign(sign), .A3(A0), .A2(B0), .A1(C0), .A0(D0), .B3(A1), .B2(B1), .B1(C1), .B0(D1), .C3(A), .C2(B),
    .C1(C), .C0(D));
  signmux4bit signmux4bit_2 (
    .sign(sign), .A3(E0), .A2(F0), .A1(G0), .A0(H0), .B3(E1), .B2(F1), .B1(G1), .B0(H1), .C3(E), .C2(F),
    .C1(G), .C0(H));
  signmux4bit signmux4bit_3 (
    .sign(sign), .A3(I0), .A2(J0), .A1(K0), .A0(L0), .B3(I1), .B2(J1), .B1(K1), .B0(L1), .C3(I), .C2(J),
    .C1(K), .C0(L));
  signmux4bit signmux4bit_4 (
    .sign(sign), .A3(M0), .A2(N0), .A1(O0), .A0(P0), .B3(M1), .B2(N1), .B1(O1), .B0(P1), .C3(M), .C2(N),
    .C1(O), .C0(P));
endmodule

module base4display (
  input  sign,
  input  A,
  input  B,
  input  C,
  input  D,
  input  E,
  input  F,
  input  G,
  input  H,
  input  I,
  input  J,
  input  K,
  input  L,
  input  M,
  input  N,
  input  O,
  input  P,
  output A2,
  output A1,
  output B1,
  output C1,
  output D1,
  output E1,
  output F1,
  output G1,
  output A0,
  output B0,
  output C0,
  output D0,
  output E0,
  output F0,
  output G0
);

  wire andcmos_1_c, andcmos_2_c, andcmos_3_c, andcmos_4_c, andcmos_5_c, andcmos_6_c, andcmos_7_c,
       andcmos_8_c, andcmos_9_c, andcmos_10_c, andcmos_11_c, andcmos_12_c, andcmos_13_c, andcmos_14_c,
       andcmos_15_c, andcmos_16_c, andcmos_17_c, andcmos_18_c, andcmos_19_c, andcmos_20_c, andcmos_21_c,
       andcmos_22_c, andcmos_23_c, andcmos_24_c, andcmos_25_c, andcmos_26_c, andcmos_27_c, andcmos_28_c,
       andcmos_29_c, andcmos_30_c, eightor_1_out_9, eightor_2_out_9, eightor_3_out_9, eightor_4_out_9,
       eightor_5_out_9, eightor_6_out_9, eightor_7_out_9, eightor_8_out_9, eightor_9_out_9, eightor_10_out_9,
       eightor_11_out_9, eightor_12_out_9, eightor_13_out_9, eightor_14_out_9, notcmos_1_c, notcmos_2_c,
       orcmos_1_c, orcmos_2_c, orcmos_3_c, orcmos_4_c, orcmos_5_c, orcmos_6_c, orcmos_7_c, orcmos_8_c,
       orcmos_9_c, orcmos_10_c, orcmos_11_c, orcmos_12_c, orcmos_13_c, orcmos_14_c, orcmos_15_c, orcmos_16_c,
       orcmos_17_c, orcmos_18_c, orcmos_19_c, orcmos_20_c, orcmos_21_c, orcmos_22_c, orcmos_23_c,
       orcmos_24_c, orcmos_25_c, orcmos_26_c, orcmos_27_c, orcmos_28_c, orcmos_29_c, orcmos_30_c,
       orcmos_31_c, orcmos_32_c, orcmos_33_c, orcmos_34_c, orcmos_35_c, orcmos_36_c, orcmos_37_c, orcmos_38_c;

  eightOR eightor_1 (
    .in_1(A), .in_2(B), .in_3(C), .in_4(D), .in_5(E), .in_6(F), .in_7(G), .in_8(H), .out_9(eightor_1_out_9));
  eightOR eightor_2 (
    .in_1(1'b0), .in_2(F), .in_3(G), .in_4(H), .in_5(I), .in_6(J), .in_7(K), .in_8(L), .out_9(eightor_2_out_9));
  eightOR eightor_3 (
    .in_1(A), .in_2(F), .in_3(G), .in_4(H), .in_5(I), .in_6(J), .in_7(K), .in_8(L), .out_9(eightor_3_out_9));
  NOTcmos notcmos_1 (.A(A), .C(notcmos_1_c));
  eightOR eightor_4 (
    .in_1(B), .in_2(C), .in_3(F), .in_4(G), .in_5(K), .in_6(L), .in_7(O), .in_8(P), .out_9(eightor_4_out_9));
  ORcmos orcmos_1 (.A(A), .B(E), .C(orcmos_1_c));
  eightOR eightor_5 (
    .in_1(A), .in_2(B), .in_3(C), .in_4(E), .in_5(F), .in_6(G), .in_7(I), .in_8(K), .out_9(eightor_5_out_9));
  eightOR eightor_6 (
    .in_1(A), .in_2(C), .in_3(E), .in_4(G), .in_5(I), .in_6(K), .in_7(M), .in_8(O), .out_9(eightor_6_out_9));
  eightOR eightor_7 (
    .in_1(A), .in_2(B), .in_3(D), .in_4(E), .in_5(F), .in_6(H), .in_7(I), .in_8(J), .out_9(eightor_7_out_9));
  eightOR eightor_8 (
    .in_1(I), .in_2(J), .in_3(K), .in_4(L), .in_5(M), .in_6(N), .in_7(O), .in_8(P), .out_9(eightor_8_out_9));
  ORcmos orcmos_2 (.A(A), .B(B), .C(orcmos_2_c));
  ORcmos orcmos_3 (.A(I), .B(J), .C(orcmos_3_c));
  eightOR eightor_9 (
    .in_1(A), .in_2(B), .in_3(C), .in_4(D), .in_5(E), .in_6(F), .in_7(G), .in_8(H), .out_9(eightor_9_out_9));
  eightOR eightor_10 (
    .in_1(C), .in_2(D), .in_3(G), .in_4(H), .in_5(K), .in_6(L), .in_7(O), .in_8(P), .out_9(eightor_10_out_9));
  ORcmos orcmos_4 (.A(A), .B(E), .C(orcmos_4_c));
  eightOR eightor_11 (
    .in_1(A), .in_2(C), .in_3(D), .in_4(E), .in_5(G), .in_6(H), .in_7(I), .in_8(K), .out_9(eightor_11_out_9));
  eightOR eightor_12 (
    .in_1(A), .in_2(B), .in_3(D), .in_4(E), .in_5(F), .in_6(H), .in_7(I), .in_8(J), .out_9(eightor_12_out_9));
  eightOR eightor_13 (
    .in_1(A), .in_2(B), .in_3(C), .in_4(E), .in_5(F), .in_6(G), .in_7(I), .in_8(K), .out_9(eightor_13_out_9));
  ORcmos orcmos_5 (.A(orcmos_1_c), .B(I), .C(orcmos_5_c));
  ORcmos orcmos_6 (.A(eightor_5_out_9), .B(L), .C(orcmos_6_c));
  ORcmos orcmos_7 (.A(eightor_7_out_9), .B(L), .C(orcmos_7_c));
  ORcmos orcmos_8 (.A(orcmos_2_c), .B(C), .C(orcmos_8_c));
  ORcmos orcmos_9 (.A(orcmos_3_c), .B(K), .C(orcmos_9_c));
  ORcmos orcmos_10 (.A(eightor_9_out_9), .B(M), .C(orcmos_10_c));
  ORcmos orcmos_11 (.A(orcmos_4_c), .B(I), .C(orcmos_11_c));
  ORcmos orcmos_12 (.A(eightor_11_out_9), .B(L), .C(orcmos_12_c));
  ORcmos orcmos_13 (.A(eightor_12_out_9), .B(L), .C(orcmos_13_c));
  ORcmos orcmos_14 (.A(eightor_13_out_9), .B(L), .C(orcmos_14_c));
  eightOR eightor_14 (
    .in_1(A), .in_2(C), .in_3(E), .in_4(G), .in_5(I), .in_6(K), .in_7(M), .in_8(O), .out_9(eightor_14_out_9));
  ORcmos orcmos_15 (.A(orcmos_5_c), .B(M), .C(orcmos_15_c));
  ORcmos orcmos_16 (.A(orcmos_6_c), .B(M), .C(orcmos_16_c));
  ORcmos orcmos_17 (.A(orcmos_7_c), .B(M), .C(orcmos_17_c));
  ORcmos orcmos_18 (.A(orcmos_8_c), .B(D), .C(orcmos_18_c));
  ORcmos orcmos_19 (.A(orcmos_9_c), .B(L), .C(orcmos_19_c));
  ORcmos orcmos_20 (.A(orcmos_10_c), .B(N), .C(orcmos_20_c));
  ORcmos orcmos_21 (.A(orcmos_11_c), .B(M), .C(orcmos_21_c));
  ORcmos orcmos_22 (.A(orcmos_12_c), .B(M), .C(orcmos_22_c));
  ORcmos orcmos_23 (.A(orcmos_13_c), .B(M), .C(orcmos_23_c));
  ORcmos orcmos_24 (.A(orcmos_14_c), .B(M), .C(orcmos_24_c));
  ORcmos orcmos_25 (.A(orcmos_16_c), .B(O), .C(orcmos_25_c));
  ORcmos orcmos_26 (.A(orcmos_17_c), .B(N), .C(orcmos_26_c));
  ORcmos orcmos_27 (.A(orcmos_18_c), .B(orcmos_19_c), .C(orcmos_27_c));
  ORcmos orcmos_28 (.A(orcmos_20_c), .B(O), .C(orcmos_28_c));
  ORcmos orcmos_29 (.A(orcmos_22_c), .B(O), .C(orcmos_29_c));
  ORcmos orcmos_30 (.A(orcmos_23_c), .B(N), .C(orcmos_30_c));
  ORcmos orcmos_31 (.A(orcmos_24_c), .B(O), .C(orcmos_31_c));
  ORcmos orcmos_32 (.A(eightor_8_out_9), .B(orcmos_18_c), .C(orcmos_32_c));
  ORcmos orcmos_33 (.A(orcmos_25_c), .B(P), .C(orcmos_33_c));
  ORcmos orcmos_34 (.A(orcmos_29_c), .B(P), .C(orcmos_34_c));
  ORcmos orcmos_35 (.A(orcmos_30_c), .B(P), .C(orcmos_35_c));
  ORcmos orcmos_36 (.A(orcmos_26_c), .B(P), .C(orcmos_36_c));
  ORcmos orcmos_37 (.A(orcmos_28_c), .B(P), .C(orcmos_37_c));
  ORcmos orcmos_38 (.A(orcmos_31_c), .B(P), .C(orcmos_38_c));
  NOTcmos notcmos_2 (.A(sign), .C(notcmos_2_c));
  ANDcmos andcmos_1 (.in_1(1'b0), .in_2(notcmos_2_c), .C(andcmos_1_c));
  ANDcmos andcmos_2 (.in_1(eightor_8_out_9), .in_2(notcmos_2_c), .C(andcmos_2_c));
  ANDcmos andcmos_3 (.in_1(orcmos_18_c), .in_2(notcmos_2_c), .C(andcmos_3_c));
  ANDcmos andcmos_4 (.in_1(orcmos_32_c), .in_2(notcmos_2_c), .C(andcmos_4_c));
  ANDcmos andcmos_5 (.in_1(eightor_1_out_9), .in_2(sign), .C(andcmos_5_c));
  ANDcmos andcmos_6 (.in_1(A), .in_2(sign), .C(andcmos_6_c));
  ANDcmos andcmos_7 (.in_1(eightor_2_out_9), .in_2(sign), .C(andcmos_7_c));
  ANDcmos andcmos_8 (.in_1(eightor_3_out_9), .in_2(sign), .C(andcmos_8_c));
  ANDcmos andcmos_9 (.in_1(1'b1), .in_2(sign), .C(andcmos_9_c));
  ANDcmos andcmos_10 (.in_1(eightor_3_out_9), .in_2(sign), .C(andcmos_10_c));
  ANDcmos andcmos_11 (.in_1(eightor_3_out_9), .in_2(sign), .C(andcmos_11_c));
  ANDcmos andcmos_12 (.in_1(notcmos_1_c), .in_2(sign), .C(andcmos_12_c));
  ANDcmos andcmos_13 (.in_1(eightor_4_out_9), .in_2(sign), .C(andcmos_13_c));
  ANDcmos andcmos_14 (.in_1(orcmos_15_c), .in_2(sign), .C(andcmos_14_c));
  ANDcmos andcmos_15 (.in_1(orcmos_38_c), .in_2(sign), .C(andcmos_15_c));
  ANDcmos andcmos_16 (.in_1(1'b1), .in_2(sign), .C(andcmos_16_c));
  ANDcmos andcmos_17 (.in_1(eightor_6_out_9), .in_2(sign), .C(andcmos_17_c));
  ANDcmos andcmos_18 (.in_1(orcmos_33_c), .in_2(sign), .C(andcmos_18_c));
  ANDcmos andcmos_19 (.in_1(orcmos_36_c), .in_2(sign), .C(andcmos_19_c));
  ANDcmos andcmos_20 (.in_1(1'b1), .in_2(notcmos_2_c), .C(andcmos_20_c));
  ANDcmos andcmos_21 (.in_1(orcmos_27_c), .in_2(notcmos_2_c), .C(andcmos_21_c));
  ANDcmos andcmos_22 (.in_1(orcmos_32_c), .in_2(notcmos_2_c), .C(andcmos_22_c));
  ANDcmos andcmos_23 (.in_1(orcmos_37_c), .in_2(notcmos_2_c), .C(andcmos_23_c));
  ANDcmos andcmos_24 (.in_1(eightor_10_out_9), .in_2(notcmos_2_c), .C(andcmos_24_c));
  ANDcmos andcmos_25 (.in_1(orcmos_21_c), .in_2(notcmos_2_c), .C(andcmos_25_c));
  ANDcmos andcmos_26 (.in_1(orcmos_34_c), .in_2(notcmos_2_c), .C(andcmos_26_c));
  ANDcmos andcmos_27 (.in_1(1'b1), .in_2(notcmos_2_c), .C(andcmos_27_c));
  ANDcmos andcmos_28 (.in_1(eightor_14_out_9), .in_2(notcmos_2_c), .C(andcmos_28_c));
  ANDcmos andcmos_29 (.in_1(orcmos_34_c), .in_2(notcmos_2_c), .C(andcmos_29_c));
  ANDcmos andcmos_30 (.in_1(orcmos_35_c), .in_2(notcmos_2_c), .C(andcmos_30_c));
  ORcmos orcmos_39 (.A(andcmos_1_c), .B(andcmos_5_c), .C(A2));
  ORcmos orcmos_40 (.A(andcmos_2_c), .B(andcmos_6_c), .C(A1));
  ORcmos orcmos_41 (.A(andcmos_3_c), .B(andcmos_7_c), .C(B1));
  ORcmos orcmos_42 (.A(andcmos_4_c), .B(andcmos_8_c), .C(C1));
  ORcmos orcmos_43 (.A(andcmos_20_c), .B(andcmos_9_c), .C(D1));
  ORcmos orcmos_44 (.A(andcmos_21_c), .B(andcmos_10_c), .C(E1));
  ORcmos orcmos_45 (.A(andcmos_22_c), .B(andcmos_11_c), .C(F1));
  ORcmos orcmos_46 (.A(andcmos_23_c), .B(andcmos_12_c), .C(G1));
  ORcmos orcmos_47 (.A(andcmos_24_c), .B(andcmos_13_c), .C(A0));
  ORcmos orcmos_48 (.A(andcmos_25_c), .B(andcmos_14_c), .C(B0));
  ORcmos orcmos_49 (.A(andcmos_26_c), .B(andcmos_15_c), .C(C0));
  ORcmos orcmos_50 (.A(andcmos_27_c), .B(andcmos_16_c), .C(D0));
  ORcmos orcmos_51 (.A(andcmos_28_c), .B(andcmos_17_c), .C(E0));
  ORcmos orcmos_52 (.A(andcmos_29_c), .B(andcmos_18_c), .C(F0));
  ORcmos orcmos_53 (.A(andcmos_30_c), .B(andcmos_19_c), .C(G0));
endmodule

module base3unsigned (
  input  A,
  input  B,
  input  C,
  input  D,
  input  E,
  input  F,
  input  G,
  input  H,
  input  I,
  input  J,
  input  K,
  input  L,
  input  M,
  input  N,
  input  O,
  input  P,
  output A2,
  output D2,
  output G2,
  output A1,
  output B1,
  output C1,
  output D1,
  output E1,
  output F1,
  output G1,
  output A0,
  output B0,
  output C0,
  output D0,
  output E0,
  output F0,
  output G0
);

  wire eightor_3_out_9, eightor_4_out_9, eightor_7_out_9, eightor_8_out_9, orcmos_1_c, orcmos_2_c,
       orcmos_3_c, orcmos_4_c, orcmos_5_c, orcmos_6_c, orcmos_9_c, orcmos_10_c, orcmos_11_c;

  eightOR eightor_1 (.in_1(J), .in_2(K), .in_3(L), .in_4(M), .in_5(N), .in_6(O), .in_7(P), .out_9(D2));  // open: in_8
  ORcmos orcmos_1 (.A(G), .B(H), .C(orcmos_1_c));
  eightOR eightor_2 (.in_1(A), .in_2(B), .in_3(C), .in_4(J), .in_5(K), .in_6(L), .out_9(B1));  // open: in_7, in_8
  eightOR eightor_3 (
    .in_1(A), .in_2(B), .in_3(C), .in_4(G), .in_5(H), .in_6(I), .in_7(J), .in_8(K), .out_9(eightor_3_out_9));
  eightOR eightor_4 (
    .in_1(A), .in_2(B), .in_3(C), .in_4(D), .in_5(E), .in_6(F), .in_7(J), .in_8(K), .out_9(eightor_4_out_9));
  eightOR eightor_5 (.in_1(C), .in_2(F), .in_3(I), .in_4(L), .in_5(O), .out_9(A0));  // open: in_6, in_7, in_8
  eightOR eightor_6 (.in_1(A), .in_2(D), .in_3(G), .in_4(J), .in_5(M), .in_6(P), .out_9(B0));  // open: in_7, in_8
  eightOR eightor_7 (
    .in_1(A), .in_2(C), .in_3(D), .in_4(F), .in_5(G), .in_6(I), .in_7(J), .in_8(L), .out_9(eightor_7_out_9));
  eightOR eightor_8 (
    .in_1(A), .in_2(B), .in_3(D), .in_4(E), .in_5(G), .in_6(H), .in_7(J), .in_8(K), .out_9(eightor_8_out_9));
  ORcmos orcmos_2 (.A(orcmos_1_c), .B(I), .C(orcmos_2_c));
  ORcmos orcmos_3 (.A(eightor_3_out_9), .B(L), .C(orcmos_3_c));
  ORcmos orcmos_4 (.A(eightor_4_out_9), .B(L), .C(orcmos_4_c));
  ORcmos orcmos_5 (.A(eightor_7_out_9), .B(M), .C(orcmos_5_c));
  ORcmos orcmos_6 (.A(eightor_8_out_9), .B(M), .C(orcmos_6_c));
  ORcmos orcmos_7 (.A(orcmos_2_c), .B(P), .C(A1));
  ORcmos orcmos_8 (.A(orcmos_3_c), .B(P), .C(C1));
  ORcmos orcmos_9 (.A(orcmos_4_c), .B(M), .C(orcmos_9_c));
  ORcmos orcmos_10 (.A(orcmos_5_c), .B(O), .C(orcmos_10_c));
  ORcmos orcmos_11 (.A(orcmos_6_c), .B(N), .C(orcmos_11_c));
  ORcmos orcmos_12 (.A(orcmos_9_c), .B(N), .C(G1));
  ORcmos orcmos_13 (.A(orcmos_10_c), .B(P), .C(C0));
  ORcmos orcmos_14 (.A(orcmos_11_c), .B(P), .C(G0));

  assign A2 = 1'b0;
  assign D0 = 1'b1;
  assign D1 = 1'b1;
  assign E0 = C0;
  assign E1 = C1;
  assign F0 = C0;
  assign F1 = C1;
  assign G2 = D2;
endmodule

module base3signed (
  input  A,
  input  B,
  input  C,
  input  D,
  input  E,
  input  F,
  input  G,
  input  H,
  input  I,
  input  J,
  input  K,
  input  L,
  input  M,
  input  N,
  input  O,
  input  P,
  output A2,
  output D2,
  output G2,
  output A1,
  output B1,
  output C1,
  output D1,
  output E1,
  output F1,
  output G1,
  output A0,
  output B0,
  output C0,
  output D0,
  output E0,
  output F0,
  output G0
);

  wire eightor_4_out_9, eightor_5_out_9, eightor_8_out_9, eightor_9_out_9, orcmos_1_c, orcmos_2_c,
       orcmos_3_c, orcmos_4_c, orcmos_6_c, orcmos_8_c;

  eightOR eightor_1 (.in_1(A), .in_2(B), .in_3(C), .in_4(D), .in_5(E), .in_6(F), .in_7(G), .in_8(H), .out_9(A2));
  eightOR eightor_2 (.in_1(A), .in_2(B), .in_3(C), .in_7(O), .in_8(P), .out_9(A1));  // open: in_4, in_5, in_6
  eightOR eightor_3 (.in_1(G), .in_2(H), .in_3(I), .in_4(J), .in_5(K), .out_9(B1));  // open: in_6, in_7, in_8
  eightOR eightor_4 (
    .in_1(A), .in_2(B), .in_3(C), .in_4(G), .in_5(H), .in_6(I), .in_7(J), .in_8(K), .out_9(eightor_4_out_9));
  eightOR eightor_5 (
    .in_1(D), .in_2(E), .in_3(F), .in_4(G), .in_5(H), .in_6(I), .in_7(J), .in_8(K), .out_9(eightor_5_out_9));
  eightOR eightor_6 (.in_1(A), .in_2(D), .in_3(G), .in_4(K), .in_5(N), .out_9(A0));  // open: in_6, in_7, in_8
  eightOR eightor_7 (.in_1(C), .in_2(F), .in_3(I), .in_4(L), .in_5(O), .out_9(B0));  // open: in_6, in_7, in_8
  eightOR eightor_8 (
    .in_1(A), .in_2(C), .in_3(D), .in_4(F), .in_5(G), .in_6(I), .in_7(K), .in_8(L), .out_9(eightor_8_out_9));
  eightOR eightor_9 (
    .in_1(B), .in_2(C), .in_3(E), .in_4(F), .in_5(H), .in_6(I), .in_7(J), .in_8(L), .out_9(eightor_9_out_9));
  ORcmos orcmos_1 (.A(eightor_4_out_9), .B(O), .C(orcmos_1_c));
  ORcmos orcmos_2 (.A(eightor_5_out_9), .B(L), .C(orcmos_2_c));
  ORcmos orcmos_3 (.A(eightor_8_out_9), .B(N), .C(orcmos_3_c));
  ORcmos orcmos_4 (.A(eightor_9_out_9), .B(M), .C(orcmos_4_c));
  ORcmos orcmos_5 (.A(orcmos_1_c), .B(P), .C(C1));
  ORcmos orcmos_6 (.A(orcmos_2_c), .B(M), .C(orcmos_6_c));
  ORcmos orcmos_7 (.A(orcmos_3_c), .B(O), .C(C0));
  ORcmos orcmos_8 (.A(orcmos_4_c), .B(O), .C(orcmos_8_c));
  ORcmos orcmos_9 (.A(orcmos_6_c), .B(N), .C(G1));
  ORcmos orcmos_10 (.A(orcmos_8_c), .B(P), .C(G0));

  assign D0 = 1'b1;
  assign D1 = 1'b1;
  assign D2 = 1'b0;
  assign E0 = C0;
  assign E1 = C1;
  assign F0 = C0;
  assign F1 = C1;
  assign G2 = 1'b0;
endmodule

module base3mux (
  input  sign,
  input  A2,
  input  in_3,
  input  D2,
  input  in_5,
  input  G2,
  input  in_7,
  input  A1,
  input  in_9,
  input  B1,
  input  in_11,
  input  C1,
  input  in_13,
  input  D1,
  input  in_15,
  input  E1,
  input  in_17,
  input  F1,
  input  in_19,
  input  G1,
  input  in_21,
  input  A0,
  input  in_23,
  input  B0,
  input  in_25,
  input  C0,
  input  in_27,
  input  D0,
  input  in_29,
  input  E0,
  input  in_31,
  input  F0,
  input  in_33,
  input  G0,
  input  in_35,
  output A2OUT,
  output D2OUT,
  output G2OUT,
  output A1OUT,
  output B1OUT,
  output C1OUT,
  output D1OUT,
  output E1OUT,
  output F1OUT,
  output G1OUT,
  output A0OUT,
  output B0OUT,
  output C0OUT,
  output D0OUT,
  output E0OUT,
  output F0OUT,
  output G0OUT
);

  wire andcmos_1_c, andcmos_2_c, notcmos_1_c;

  NOTcmos notcmos_1 (.A(sign), .C(notcmos_1_c));
  ANDcmos andcmos_1 (.in_1(notcmos_1_c), .in_2(G0), .C(andcmos_1_c));
  ANDcmos andcmos_2 (.in_1(sign), .in_2(in_35), .C(andcmos_2_c));
  signmux16bit signmux16bit_1 (
    .sign(sign), .A0(A2), .A1(in_3), .B0(D2), .B1(in_5), .C0(G2), .C1(in_7), .D0(A1), .D1(in_9), .E0(B1),
    .E1(in_11), .F0(C1), .F1(in_13), .G0(D1), .G1(in_15), .H0(E1), .H1(in_17), .I0(F1), .I1(in_19), .J0(G1),
    .J1(in_21), .K0(A0), .K1(in_23), .L0(B0), .L1(in_25), .M0(C0), .M1(in_27), .N0(D0), .N1(in_29), .O0(E0),
    .O1(in_31), .P0(F0), .P1(in_33), .A(A2OUT), .B(D2OUT), .C(G2OUT), .D(A1OUT), .E(B1OUT), .F(C1OUT),
    .G(D1OUT), .H(E1OUT), .I(F1OUT), .J(G1OUT), .K(A0OUT), .L(B0OUT), .M(C0OUT), .N(D0OUT), .O(E0OUT),
    .P(F0OUT));
  ORcmos orcmos_1 (.A(andcmos_1_c), .B(andcmos_2_c), .C(G0OUT));
endmodule

module base3display (
  input  sign,
  input  A,
  input  B,
  input  C,
  input  D,
  input  E,
  input  F,
  input  G,
  input  H,
  input  I,
  input  J,
  input  K,
  input  L,
  input  M,
  input  N,
  input  O,
  input  P,
  output A2,
  output D2,
  output G2,
  output A1,
  output B1,
  output C1,
  output D1,
  output E1,
  output F1,
  output G1,
  output A0,
  output B0,
  output C0,
  output D0,
  output E0,
  output F0,
  output G0
);

  wire base3signed_1_a0, base3signed_1_a1, base3signed_1_a2, base3signed_1_b0, base3signed_1_b1,
       base3signed_1_c0, base3signed_1_c1, base3signed_1_d0, base3signed_1_d1, base3signed_1_d2,
       base3signed_1_e0, base3signed_1_e1, base3signed_1_f0, base3signed_1_f1, base3signed_1_g0,
       base3signed_1_g1, base3signed_1_g2, base3unsigned_1_a0, base3unsigned_1_a1, base3unsigned_1_a2,
       base3unsigned_1_b0, base3unsigned_1_b1, base3unsigned_1_c0, base3unsigned_1_c1, base3unsigned_1_d0,
       base3unsigned_1_d1, base3unsigned_1_d2, base3unsigned_1_e0, base3unsigned_1_e1, base3unsigned_1_f0,
       base3unsigned_1_f1, base3unsigned_1_g0, base3unsigned_1_g1, base3unsigned_1_g2;

  base3unsigned base3unsigned_1 (
    .A(A), .B(B), .C(C), .D(D), .E(E), .F(F), .G(G), .H(H), .I(I), .J(J), .K(K), .L(L), .M(M), .N(N), .O(O),
    .P(P), .A2(base3unsigned_1_a2), .D2(base3unsigned_1_d2), .G2(base3unsigned_1_g2),
    .A1(base3unsigned_1_a1), .B1(base3unsigned_1_b1), .C1(base3unsigned_1_c1), .D1(base3unsigned_1_d1),
    .E1(base3unsigned_1_e1), .F1(base3unsigned_1_f1), .G1(base3unsigned_1_g1), .A0(base3unsigned_1_a0),
    .B0(base3unsigned_1_b0), .C0(base3unsigned_1_c0), .D0(base3unsigned_1_d0), .E0(base3unsigned_1_e0),
    .F0(base3unsigned_1_f0), .G0(base3unsigned_1_g0));
  base3signed base3signed_1 (
    .A(A), .B(B), .C(C), .D(D), .E(E), .F(F), .G(G), .H(H), .I(I), .J(J), .K(K), .L(L), .M(M), .N(N), .O(O),
    .P(P), .A2(base3signed_1_a2), .D2(base3signed_1_d2), .G2(base3signed_1_g2), .A1(base3signed_1_a1),
    .B1(base3signed_1_b1), .C1(base3signed_1_c1), .D1(base3signed_1_d1), .E1(base3signed_1_e1),
    .F1(base3signed_1_f1), .G1(base3signed_1_g1), .A0(base3signed_1_a0), .B0(base3signed_1_b0),
    .C0(base3signed_1_c0), .D0(base3signed_1_d0), .E0(base3signed_1_e0), .F0(base3signed_1_f0),
    .G0(base3signed_1_g0));
  base3mux base3mux_1 (
    .sign(sign), .A2(base3unsigned_1_a2), .in_3(base3signed_1_a2), .D2(base3unsigned_1_d2),
    .in_5(base3signed_1_d2), .G2(base3unsigned_1_g2), .in_7(base3signed_1_g2), .A1(base3unsigned_1_a1),
    .in_9(base3signed_1_a1), .B1(base3unsigned_1_b1), .in_11(base3signed_1_b1), .C1(base3unsigned_1_c1),
    .in_13(base3signed_1_c1), .D1(base3unsigned_1_d1), .in_15(base3signed_1_d1), .E1(base3unsigned_1_e1),
    .in_17(base3signed_1_e1), .F1(base3unsigned_1_f1), .in_19(base3signed_1_f1), .G1(base3unsigned_1_g1),
    .in_21(base3signed_1_g1), .A0(base3unsigned_1_a0), .in_23(base3signed_1_a0), .B0(base3unsigned_1_b0),
    .in_25(base3signed_1_b0), .C0(base3unsigned_1_c0), .in_27(base3signed_1_c0), .D0(base3unsigned_1_d0),
    .in_29(base3signed_1_d0), .E0(base3unsigned_1_e0), .in_31(base3signed_1_e0), .F0(base3unsigned_1_f0),
    .in_33(base3signed_1_f0), .G0(base3unsigned_1_g0), .in_35(base3signed_1_g0), .A2OUT(A2), .D2OUT(D2),
    .G2OUT(G2), .A1OUT(A1), .B1OUT(B1), .C1OUT(C1), .D1OUT(D1), .E1OUT(E1), .F1OUT(F1), .G1OUT(G1),
    .A0OUT(A0), .B0OUT(B0), .C0OUT(C0), .D0OUT(D0), .E0OUT(E0), .F0OUT(F0), .G0OUT(G0));
endmodule

module main (
  input  sign,
  input  sub,
  output S3,
  output S2,
  output S1,
  output S0,
  output Overflow
);

  wire andcmos_1_c, andcmos_2_c, andcmos_3_c, andcmos_4_c, andcmos_5_c, andcmos_6_c, andcmos_7_c,
       andcmos_8_c, andcmos_9_c, andcmos_10_c, andcmos_11_c, andcmos_12_c, andcmos_13_c, andcmos_14_c,
       andcmos_15_c, andcmos_16_c, andcmos_17_c, base3display_1_a0, base3display_1_a1, base3display_1_a2,
       base3display_1_b0, base3display_1_b1, base3display_1_c0, base3display_1_c1, base3display_1_d0,
       base3display_1_d1, base3display_1_d2, base3display_1_e0, base3display_1_e1, base3display_1_f0,
       base3display_1_f1, base3display_1_g0, base3display_1_g1, base3display_1_g2, base4display_1_a0,
       base4display_1_a1, base4display_1_a2, base4display_1_b0, base4display_1_b1, base4display_1_c0,
       base4display_1_c1, base4display_1_d0, base4display_1_d1, base4display_1_e0, base4display_1_e1,
       base4display_1_f0, base4display_1_f1, base4display_1_g0, base4display_1_g1, base4display_2_a0,
       base4display_2_a1, base4display_2_a2, base4display_2_b0, base4display_2_b1, base4display_2_c0,
       base4display_2_c1, base4display_2_d0, base4display_2_d1, base4display_2_e0, base4display_2_e1,
       base4display_2_f0, base4display_2_f1, base4display_2_g0, base4display_2_g1, dipswitch_1_sw1,
       dipswitch_1_sw2, dipswitch_1_sw3, dipswitch_1_sw4, dipswitch_1_sw5, dipswitch_1_sw6, dipswitch_1_sw7,
       dipswitch_1_sw8, dipswitch_1_sw9, dipswitch_1_sw10, dipswitch_1_sw11, dipswitch_1_sw12,
       dipswitch_1_sw13, dipswitch_1_sw14, dipswitch_1_sw15, dipswitch_1_sw16, dipswitch_2_sw1,
       dipswitch_2_sw2, dipswitch_2_sw3, dipswitch_2_sw4, dipswitch_2_sw5, dipswitch_2_sw6, dipswitch_2_sw7,
       dipswitch_2_sw8, dipswitch_2_sw9, dipswitch_2_sw10, dipswitch_2_sw11, dipswitch_2_sw12,
       dipswitch_2_sw13, dipswitch_2_sw14, dipswitch_2_sw15, dipswitch_2_sw16, notcmos_1_c, orcmos_1_c,
       orcmos_2_c, orcmos_3_c, orcmos_4_c, orcmos_5_c, signedinput_1_b0, signedinput_1_b1, signedinput_1_b2,
       signedinput_1_b3, signedinput_2_b0, signedinput_2_b1, signedinput_2_b2, signedinput_2_b3,
       signedoutput_1_a, signedoutput_1_b, signedoutput_1_c, signedoutput_1_d, signedoutput_1_e,
       signedoutput_1_f, signedoutput_1_g, signedoutput_1_h, signedoutput_1_i, signedoutput_1_j,
       signedoutput_1_k, signedoutput_1_l, signedoutput_1_m, signedoutput_1_n, signedoutput_1_o,
       signedoutput_1_p, signmux4bit_1_c0, signmux4bit_1_c1, signmux4bit_1_c2, signmux4bit_1_c3,
       signmux4bit_2_c0, signmux4bit_2_c1, signmux4bit_2_c2, signmux4bit_2_c3, signmux16bit_1_a,
       signmux16bit_1_b, signmux16bit_1_c, signmux16bit_1_d, signmux16bit_1_e, signmux16bit_1_f,
       signmux16bit_1_g, signmux16bit_1_h, signmux16bit_1_i, signmux16bit_1_j, signmux16bit_1_k,
       signmux16bit_1_l, signmux16bit_1_m, signmux16bit_1_n, signmux16bit_1_o, signmux16bit_1_p,
       unsignedinput_1_b0, unsignedinput_1_b1, unsignedinput_1_b2, unsignedinput_1_b3, unsignedinput_2_b0,
       unsignedinput_2_b1, unsignedinput_2_b2, unsignedinput_2_b3, unsignedoutput_1_a, unsignedoutput_1_b,
       unsignedoutput_1_c, unsignedoutput_1_d, unsignedoutput_1_e, unsignedoutput_1_f, unsignedoutput_1_g,
       unsignedoutput_1_h, unsignedoutput_1_i, unsignedoutput_1_j, unsignedoutput_1_k, unsignedoutput_1_l,
       unsignedoutput_1_m, unsignedoutput_1_n, unsignedoutput_1_o, unsignedoutput_1_p;

  DipSwitch #(.number(16)) dipswitch_1 (
    .sw1(dipswitch_1_sw1), .sw2(dipswitch_1_sw2), .sw3(dipswitch_1_sw3), .sw4(dipswitch_1_sw4),
    .sw5(dipswitch_1_sw5), .sw6(dipswitch_1_sw6), .sw7(dipswitch_1_sw7), .sw8(dipswitch_1_sw8),
    .sw9(dipswitch_1_sw9), .sw10(dipswitch_1_sw10), .sw11(dipswitch_1_sw11), .sw12(dipswitch_1_sw12),
    .sw13(dipswitch_1_sw13), .sw14(dipswitch_1_sw14), .sw15(dipswitch_1_sw15), .sw16(dipswitch_1_sw16));
  DipSwitch #(.number(16)) dipswitch_2 (
    .sw1(dipswitch_2_sw1), .sw2(dipswitch_2_sw2), .sw3(dipswitch_2_sw3), .sw4(dipswitch_2_sw4),
    .sw5(dipswitch_2_sw5), .sw6(dipswitch_2_sw6), .sw7(dipswitch_2_sw7), .sw8(dipswitch_2_sw8),
    .sw9(dipswitch_2_sw9), .sw10(dipswitch_2_sw10), .sw11(dipswitch_2_sw11), .sw12(dipswitch_2_sw12),
    .sw13(dipswitch_2_sw13), .sw14(dipswitch_2_sw14), .sw15(dipswitch_2_sw15), .sw16(dipswitch_2_sw16));
  base4display base4display_1 (
    .sign(sign), .A(dipswitch_1_sw1), .B(dipswitch_1_sw2), .C(dipswitch_1_sw3), .D(dipswitch_1_sw4),
    .E(dipswitch_1_sw5), .F(dipswitch_1_sw6), .G(dipswitch_1_sw7), .H(dipswitch_1_sw8), .I(dipswitch_1_sw9),
    .J(dipswitch_1_sw10), .K(dipswitch_1_sw11), .L(dipswitch_1_sw12), .M(dipswitch_1_sw13),
    .N(dipswitch_1_sw14), .O(dipswitch_1_sw15), .P(dipswitch_1_sw16), .A2(base4display_1_a2),
    .A1(base4display_1_a1), .B1(base4display_1_b1), .C1(base4display_1_c1), .D1(base4display_1_d1),
    .E1(base4display_1_e1), .F1(base4display_1_f1), .G1(base4display_1_g1), .A0(base4display_1_a0),
    .B0(base4display_1_b0), .C0(base4display_1_c0), .D0(base4display_1_d0), .E0(base4display_1_e0),
    .F0(base4display_1_f0), .G0(base4display_1_g0));
  base4display base4display_2 (
    .sign(sign), .A(dipswitch_2_sw1), .B(dipswitch_2_sw2), .C(dipswitch_2_sw3), .D(dipswitch_2_sw4),
    .E(dipswitch_2_sw5), .F(dipswitch_2_sw6), .G(dipswitch_2_sw7), .H(dipswitch_2_sw8), .I(dipswitch_2_sw9),
    .J(dipswitch_2_sw10), .K(dipswitch_2_sw11), .L(dipswitch_2_sw12), .M(dipswitch_2_sw13),
    .N(dipswitch_2_sw14), .O(dipswitch_2_sw15), .P(dipswitch_2_sw16), .A2(base4display_2_a2),
    .A1(base4display_2_a1), .B1(base4display_2_b1), .C1(base4display_2_c1), .D1(base4display_2_d1),
    .E1(base4display_2_e1), .F1(base4display_2_f1), .G1(base4display_2_g1), .A0(base4display_2_a0),
    .B0(base4display_2_b0), .C0(base4display_2_c0), .D0(base4display_2_d0), .E0(base4display_2_e0),
    .F0(base4display_2_f0), .G0(base4display_2_g0));
  _7_Segment_Display u_7_segment_display_1 (.g(base4display_1_a2));  // open: f, a, b, e, d, c, dp
  _7_Segment_Display u_7_segment_display_2 (.g(base4display_2_a2));  // open: f, a, b, e, d, c, dp
  unsignedinput unsignedinput_1 (
    .A(dipswitch_1_sw1), .B(dipswitch_1_sw2), .C(dipswitch_1_sw3), .D(dipswitch_1_sw4), .E(dipswitch_1_sw5),
    .F(dipswitch_1_sw6), .G(dipswitch_1_sw7), .H(dipswitch_1_sw8), .I(dipswitch_1_sw9), .J(dipswitch_1_sw10),
    .K(dipswitch_1_sw11), .L(dipswitch_1_sw12), .M(dipswitch_1_sw13), .N(dipswitch_1_sw14),
    .O(dipswitch_1_sw15), .P(dipswitch_1_sw16), .B3(unsignedinput_1_b3), .B2(unsignedinput_1_b2),
    .B1(unsignedinput_1_b1), .B0(unsignedinput_1_b0));
  signedinput signedinput_1 (
    .A(dipswitch_1_sw1), .B(dipswitch_1_sw2), .C(dipswitch_1_sw3), .D(dipswitch_1_sw4), .E(dipswitch_1_sw5),
    .F(dipswitch_1_sw6), .G(dipswitch_1_sw7), .H(dipswitch_1_sw8), .I(dipswitch_1_sw9), .J(dipswitch_1_sw10),
    .K(dipswitch_1_sw11), .L(dipswitch_1_sw12), .M(dipswitch_1_sw13), .N(dipswitch_1_sw14),
    .O(dipswitch_1_sw15), .P(dipswitch_1_sw16), .B3(signedinput_1_b3), .B2(signedinput_1_b2),
    .B1(signedinput_1_b1), .B0(signedinput_1_b0));
  _7_Segment_Display u_7_segment_display_3 (
    .g(base4display_1_a1), .f(base4display_1_b1), .a(base4display_1_c1), .b(base4display_1_d1),
    .e(base4display_1_e1), .d(base4display_1_f1), .c(base4display_1_g1));  // open: dp
  _7_Segment_Display u_7_segment_display_4 (
    .g(base4display_1_a0), .f(base4display_1_b0), .a(base4display_1_c0), .b(base4display_1_d0),
    .e(base4display_1_e0), .d(base4display_1_f0), .c(base4display_1_g0));  // open: dp
  _7_Segment_Display u_7_segment_display_5 (
    .g(base4display_2_a1), .f(base4display_2_b1), .a(base4display_2_c1), .b(base4display_2_d1),
    .e(base4display_2_e1), .d(base4display_2_f1), .c(base4display_2_g1));  // open: dp
  _7_Segment_Display u_7_segment_display_6 (
    .g(base4display_2_a0), .f(base4display_2_b0), .a(base4display_2_c0), .b(base4display_2_d0),
    .e(base4display_2_e0), .d(base4display_2_f0), .c(base4display_2_g0));  // open: dp
  unsignedinput unsignedinput_2 (
    .A(dipswitch_2_sw1), .B(dipswitch_2_sw2), .C(dipswitch_2_sw3), .D(dipswitch_2_sw4), .E(dipswitch_2_sw5),
    .F(dipswitch_2_sw6), .G(dipswitch_2_sw7), .H(dipswitch_2_sw8), .I(dipswitch_2_sw9), .J(dipswitch_2_sw10),
    .K(dipswitch_2_sw11), .L(dipswitch_2_sw12), .M(dipswitch_2_sw13), .N(dipswitch_2_sw14),
    .O(dipswitch_2_sw15), .P(dipswitch_2_sw16), .B3(unsignedinput_2_b3), .B2(unsignedinput_2_b2),
    .B1(unsignedinput_2_b1), .B0(unsignedinput_2_b0));
  signedinput signedinput_2 (
    .A(dipswitch_2_sw1), .B(dipswitch_2_sw2), .C(dipswitch_2_sw3), .D(dipswitch_2_sw4), .E(dipswitch_2_sw5),
    .F(dipswitch_2_sw6), .G(dipswitch_2_sw7), .H(dipswitch_2_sw8), .I(dipswitch_2_sw9), .J(dipswitch_2_sw10),
    .K(dipswitch_2_sw11), .L(dipswitch_2_sw12), .M(dipswitch_2_sw13), .N(dipswitch_2_sw14),
    .O(dipswitch_2_sw15), .P(dipswitch_2_sw16), .B3(signedinput_2_b3), .B2(signedinput_2_b2),
    .B1(signedinput_2_b1), .B0(signedinput_2_b0));
  signmux4bit signmux4bit_1 (
    .sign(sign), .A3(unsignedinput_1_b3), .A2(unsignedinput_1_b2), .A1(unsignedinput_1_b1),
    .A0(unsignedinput_1_b0), .B3(signedinput_1_b3), .B2(signedinput_1_b2), .B1(signedinput_1_b1),
    .B0(signedinput_1_b0), .C3(signmux4bit_1_c3), .C2(signmux4bit_1_c2), .C1(signmux4bit_1_c1),
    .C0(signmux4bit_1_c0));
  signmux4bit signmux4bit_2 (
    .sign(sign), .A3(unsignedinput_2_b3), .A2(unsignedinput_2_b2), .A1(unsignedinput_2_b1),
    .A0(unsignedinput_2_b0), .B3(signedinput_2_b3), .B2(signedinput_2_b2), .B1(signedinput_2_b1),
    .B0(signedinput_2_b0), .C3(signmux4bit_2_c3), .C2(signmux4bit_2_c2), .C1(signmux4bit_2_c1),
    .C0(signmux4bit_2_c0));
  fourbitadder fourbitadder_1 (
    .sign(sign), .A3(signmux4bit_1_c3), .A2(signmux4bit_1_c2), .A1(signmux4bit_1_c1), .A0(signmux4bit_1_c0),
    .B3(signmux4bit_2_c3), .B2(signmux4bit_2_c2), .B1(signmux4bit_2_c1), .B0(signmux4bit_2_c0), .Cin(sub),
    .S0(S0), .S1(S1), .S2(S2), .S3(S3), .overflow(Overflow));  // open: Cout
  unsignedoutput unsignedoutput_1 (
    .B3(S3), .B2(S2), .B1(S1), .B0(S0), .A(unsignedoutput_1_a), .B(unsignedoutput_1_b),
    .C(unsignedoutput_1_c), .D(unsignedoutput_1_d), .E(unsignedoutput_1_e), .F(unsignedoutput_1_f),
    .G(unsignedoutput_1_g), .H(unsignedoutput_1_h), .I(unsignedoutput_1_i), .J(unsignedoutput_1_j),
    .K(unsignedoutput_1_k), .L(unsignedoutput_1_l), .M(unsignedoutput_1_m), .N(unsignedoutput_1_n),
    .O(unsignedoutput_1_o), .P(unsignedoutput_1_p));
  signedoutput signedoutput_1 (
    .B3(S3), .B2(S2), .B1(S1), .B0(S0), .A(signedoutput_1_a), .B(signedoutput_1_b), .C(signedoutput_1_c),
    .D(signedoutput_1_d), .E(signedoutput_1_e), .F(signedoutput_1_f), .G(signedoutput_1_g),
    .H(signedoutput_1_h), .I(signedoutput_1_i), .J(signedoutput_1_j), .K(signedoutput_1_k),
    .L(signedoutput_1_l), .M(signedoutput_1_m), .N(signedoutput_1_n), .O(signedoutput_1_o),
    .P(signedoutput_1_p));
  signmux16bit signmux16bit_1 (
    .sign(sign), .A0(unsignedoutput_1_a), .A1(signedoutput_1_a), .B0(unsignedoutput_1_b),
    .B1(signedoutput_1_b), .C0(unsignedoutput_1_c), .C1(signedoutput_1_c), .D0(unsignedoutput_1_d),
    .D1(signedoutput_1_d), .E0(unsignedoutput_1_e), .E1(signedoutput_1_e), .F0(unsignedoutput_1_f),
    .F1(signedoutput_1_f), .G0(unsignedoutput_1_g), .G1(signedoutput_1_g), .H0(unsignedoutput_1_h),
    .H1(signedoutput_1_h), .I0(unsignedoutput_1_i), .I1(signedoutput_1_i), .J0(unsignedoutput_1_j),
    .J1(signedoutput_1_j), .K0(unsignedoutput_1_k), .K1(signedoutput_1_k), .L0(unsignedoutput_1_l),
    .L1(signedoutput_1_l), .M0(unsignedoutput_1_m), .M1(signedoutput_1_m), .N0(unsignedoutput_1_n),
    .N1(signedoutput_1_n), .O0(unsignedoutput_1_o), .O1(signedoutput_1_o), .P0(unsignedoutput_1_p),
    .P1(signedoutput_1_p), .A(signmux16bit_1_a), .B(signmux16bit_1_b), .C(signmux16bit_1_c),
    .D(signmux16bit_1_d), .E(signmux16bit_1_e), .F(signmux16bit_1_f), .G(signmux16bit_1_g),
    .H(signmux16bit_1_h), .I(signmux16bit_1_i), .J(signmux16bit_1_j), .K(signmux16bit_1_k),
    .L(signmux16bit_1_l), .M(signmux16bit_1_m), .N(signmux16bit_1_n), .O(signmux16bit_1_o),
    .P(signmux16bit_1_p));
  NOTcmos notcmos_1 (.A(Overflow), .C(notcmos_1_c));
  base3display base3display_1 (
    .sign(sign), .A(signmux16bit_1_a), .B(signmux16bit_1_b), .C(signmux16bit_1_c), .D(signmux16bit_1_d),
    .E(signmux16bit_1_e), .F(signmux16bit_1_f), .G(signmux16bit_1_g), .H(signmux16bit_1_h),
    .I(signmux16bit_1_i), .J(signmux16bit_1_j), .K(signmux16bit_1_k), .L(signmux16bit_1_l),
    .M(signmux16bit_1_m), .N(signmux16bit_1_n), .O(signmux16bit_1_o), .P(signmux16bit_1_p),
    .A2(base3display_1_a2), .D2(base3display_1_d2), .G2(base3display_1_g2), .A1(base3display_1_a1),
    .B1(base3display_1_b1), .C1(base3display_1_c1), .D1(base3display_1_d1), .E1(base3display_1_e1),
    .F1(base3display_1_f1), .G1(base3display_1_g1), .A0(base3display_1_a0), .B0(base3display_1_b0),
    .C0(base3display_1_c0), .D0(base3display_1_d0), .E0(base3display_1_e0), .F0(base3display_1_f0),
    .G0(base3display_1_g0));
  ANDcmos andcmos_1 (.in_1(base3display_1_a2), .in_2(notcmos_1_c), .C(andcmos_1_c));
  ANDcmos andcmos_2 (.in_1(base3display_1_d2), .in_2(notcmos_1_c), .C(andcmos_2_c));
  ANDcmos andcmos_3 (.in_1(base3display_1_g2), .in_2(notcmos_1_c), .C(andcmos_3_c));
  ANDcmos andcmos_4 (.in_1(base3display_1_a1), .in_2(notcmos_1_c), .C(andcmos_4_c));
  ANDcmos andcmos_5 (.in_1(base3display_1_b1), .in_2(notcmos_1_c), .C(andcmos_5_c));
  ANDcmos andcmos_6 (.in_1(base3display_1_c1), .in_2(notcmos_1_c), .C(andcmos_6_c));
  ANDcmos andcmos_7 (.in_1(base3display_1_d1), .in_2(notcmos_1_c), .C(andcmos_7_c));
  ANDcmos andcmos_8 (.in_1(base3display_1_e1), .in_2(notcmos_1_c), .C(andcmos_8_c));
  ANDcmos andcmos_9 (.in_1(base3display_1_f1), .in_2(notcmos_1_c), .C(andcmos_9_c));
  ANDcmos andcmos_10 (.in_1(base3display_1_g1), .in_2(notcmos_1_c), .C(andcmos_10_c));
  ANDcmos andcmos_11 (.in_1(base3display_1_a0), .in_2(notcmos_1_c), .C(andcmos_11_c));
  ANDcmos andcmos_12 (.in_1(base3display_1_b0), .in_2(notcmos_1_c), .C(andcmos_12_c));
  ANDcmos andcmos_13 (.in_1(base3display_1_c0), .in_2(notcmos_1_c), .C(andcmos_13_c));
  ANDcmos andcmos_14 (.in_1(base3display_1_d0), .in_2(notcmos_1_c), .C(andcmos_14_c));
  ANDcmos andcmos_15 (.in_1(base3display_1_e0), .in_2(notcmos_1_c), .C(andcmos_15_c));
  ANDcmos andcmos_16 (.in_1(base3display_1_f0), .in_2(notcmos_1_c), .C(andcmos_16_c));
  ANDcmos andcmos_17 (.in_1(base3display_1_g0), .in_2(notcmos_1_c), .C(andcmos_17_c));
  _7_Segment_Display u_7_segment_display_7 (
    .g(orcmos_1_c), .f(Overflow), .a(Overflow), .b(andcmos_2_c), .e(Overflow), .d(Overflow), .c(andcmos_3_c));  // open: dp
  _7_Segment_Display u_7_segment_display_8 (
    .g(orcmos_2_c), .f(andcmos_5_c), .a(andcmos_6_c), .b(andcmos_7_c), .e(orcmos_3_c), .d(andcmos_9_c),
    .c(andcmos_10_c));  // open: dp
  _7_Segment_Display u_7_segment_display_9 (
    .g(orcmos_4_c), .f(andcmos_12_c), .a(andcmos_13_c), .b(andcmos_14_c), .e(orcmos_5_c), .d(andcmos_16_c),
    .c(andcmos_17_c));  // open: dp
  ORcmos orcmos_1 (.A(andcmos_1_c), .B(Overflow), .C(orcmos_1_c));
  ORcmos orcmos_2 (.A(andcmos_4_c), .B(Overflow), .C(orcmos_2_c));
  ORcmos orcmos_3 (.A(andcmos_8_c), .B(Overflow), .C(orcmos_3_c));
  ORcmos orcmos_4 (.A(andcmos_11_c), .B(Overflow), .C(orcmos_4_c));
  ORcmos orcmos_5 (.A(andcmos_15_c), .B(Overflow), .C(orcmos_5_c));
endmodule
